// Logisim project ALBER_Tunnitoo_28_01.circ as structural Verilog: 1 circuit, main circuit main
module main (
);

  wire clock_1_out;
  wire [4:0] rom_1_data, shift_register_1_q0, shift_register_1_q1, shift_register_1_q2, shift_register_1_q3,
       shift_register_1_q4, shift_register_1_q5, shift_register_1_q6, shift_register_1_q7;
  wire [6:0] counter_1_q;

  Counter #(.width(7), .max('h7f)) counter_1 (.Q(counter_1_q), .clk(clock_1_out));  // open: load, D, count, carry, clr
  ROM #(.addrWidth(7), .dataWidth(5)) rom_1 (.addr(counter_1_q), .data(rom_1_data));  // open: sel
  Clock clock_1 (.out(clock_1_out));
  Shift_Register #(.width(5)) shift_register_1 (
    .in(rom_1_data), .clk(clock_1_out), .q0(shift_register_1_q0), .q1(shift_register_1_q1),
    .q2(shift_register_1_q2), .q3(shift_register_1_q3), .q4(shift_register_1_q4), .q5(shift_register_1_q5),
    .q6(shift_register_1_q6), .q7(shift_register_1_q7));  // open: shift, out, load, clr, d0, d1, d2, d3, d4, d5, d6, d7
  DotMatrix #(.matrixcols(8), .matrixrows(5)) dotmatrix_1 (
    .col0(shift_register_1_q7), .col1(shift_register_1_q6), .col2(shift_register_1_q5),
    .col3(shift_register_1_q4), .col4(shift_register_1_q3), .col5(shift_register_1_q2),
    .col6(shift_register_1_q1), .col7(shift_register_1_q0));

  // Notes on the sheet:
  //   contents of rom_1 (hex, n*v repeats v):
  //   10 1f 10 0 1f 11 1f 0 1f 8 4 8 1f 0 1f 0 0 1f 8 4 8 1f 0 f 12 f 0 1f 16 d 0 1f 4 1b 0 1f 1 1f 0 1d
  //   15 17 0 0 f 12 f 0 1f 1 1 0 1f 15 e 0 1f 15 0 1f 16 d
endmodule
