// Logisim project TA18E.circ as structural Verilog: 1 circuit, main circuit main
module main (
);

  wire clock_1_out, counter_1_carry, counter_2_carry, counter_3_carry, counter_4_carry, counter_6_carry,
       H_out, M_out, or_1_out, or_2_out;
  wire [3:0] counter_1_q, counter_2_q, counter_3_q, counter_4_q, counter_5_q, counter_6_q;

  Clock clock_1 (.out(clock_1_out));
  Button M (.out(M_out));
  Button H (.out(H_out));
  Counter #(.width(4), .max('h6)) counter_1 (
    .Q(counter_1_q), .carry(counter_1_carry), .clk(counter_2_carry), .clr(counter_1_carry));  // open: load, D, count
  Counter #(.width(4), .max('ha)) counter_2 (
    .Q(counter_2_q), .carry(counter_2_carry), .clk(clock_1_out), .clr(counter_2_carry));  // open: load, D, count
  Counter #(.width(4), .max('ha)) counter_3 (
    .Q(counter_3_q), .carry(counter_3_carry), .clk(or_1_out), .clr(counter_3_carry));  // open: load, D, count
  or or_1 (or_1_out, counter_1_carry, M_out);
  Hex_Digit_Display hex_digit_display_1 (.value(counter_5_q));  // open: dp
  Counter #(.width(4), .max('h6)) counter_4 (
    .Q(counter_4_q), .carry(counter_4_carry), .clk(counter_3_carry), .clr(counter_4_carry));  // open: load, D, count
  or or_2 (or_2_out, counter_4_carry, H_out);
  Hex_Digit_Display hex_digit_display_2 (.value(counter_6_q), .dp(clock_1_out));
  Counter #(.width(4), .max('h2)) counter_5 (
    .Q(counter_5_q), .clk(counter_6_carry));  // open: load, D, count, carry, clr
  Counter #(.width(4), .max('ha)) counter_6 (
    .Q(counter_6_q), .carry(counter_6_carry), .clk(or_2_out), .clr(counter_6_carry));  // open: load, D, count
  Hex_Digit_Display hex_digit_display_3 (.value(counter_3_q), .dp(clock_1_out));
  Hex_Digit_Display hex_digit_display_4 (.value(counter_4_q));  // open: dp
  Hex_Digit_Display hex_digit_display_5 (.value(counter_2_q));  // open: dp
  Hex_Digit_Display hex_digit_display_6 (.value(counter_1_q));  // open: dp
endmodule
