// Logisim project ALBER.circ as structural Verilog: 2 circuits, main circuit Kell
module main (
);

  wire H_out, kell_1_out_9, M_out;
  wire [3:0] kell_1_out_3, kell_1_out_4, kell_1_out_5, kell_1_out_6, kell_1_out_7, kell_1_out_8;

  Hex_Digit_Display hex_digit_display_1 (.value(kell_1_out_4), .dp(kell_1_out_9));
  Hex_Digit_Display hex_digit_display_2 (.value(kell_1_out_3));  // open: dp
  Kell kell_1 (
    .M(M_out), .H(H_out), .out_9(kell_1_out_9), .out_3(kell_1_out_3), .out_4(kell_1_out_4),
    .out_5(kell_1_out_5), .out_6(kell_1_out_6), .out_7(kell_1_out_7), .out_8(kell_1_out_8));
  Button M (.out(M_out));
  Hex_Digit_Display hex_digit_display_3 (.value(kell_1_out_5));  // open: dp
  Hex_Digit_Display hex_digit_display_4 (.value(kell_1_out_6), .dp(kell_1_out_9));
  Button H (.out(H_out));
  Hex_Digit_Display hex_digit_display_5 (.value(kell_1_out_7));  // open: dp
  Hex_Digit_Display hex_digit_display_6 (.value(kell_1_out_8));  // open: dp
endmodule

module Kell (
  input  M,
  input  H,
  output [3:0] out_3,
  output [3:0] out_4,
  output [3:0] out_5,
  output [3:0] out_6,
  output [3:0] out_7,
  output [3:0] out_8,
  output out_9
);

  wire counter_1_carry, counter_2_carry, counter_3_carry, counter_4_carry, counter_5_carry, counter_6_carry,
       or_1_out, or_2_out, or_3_out;

  Clock clock_1 (.out(out_9));
  Counter #(.width(4), .max('ha)) counter_1 (
    .Q(out_8), .carry(counter_1_carry), .clk(out_9), .clr(counter_1_carry));  // open: load, D, count
  Counter #(.width(4), .max('h6)) counter_2 (
    .Q(out_7), .carry(counter_2_carry), .clk(counter_1_carry), .clr(counter_2_carry));  // open: load, D, count
  Counter #(.width(4), .max('ha)) counter_3 (
    .Q(out_6), .carry(counter_3_carry), .clk(or_1_out), .clr(counter_3_carry));  // open: load, D, count
  or or_1 (or_1_out, counter_2_carry, M);
  Counter #(.width(4), .max('h6)) counter_4 (
    .Q(out_5), .carry(counter_4_carry), .clk(counter_3_carry), .clr(counter_4_carry));  // open: load, D, count
  Counter #(.width(4), .max('ha)) counter_5 (
    .Q(out_4), .carry(counter_5_carry), .clk(or_3_out), .clr(or_2_out));  // open: load, D, count
  or or_2 (or_2_out, counter_5_carry, counter_6_carry);
  or or_3 (or_3_out, counter_4_carry, H);
  Counter #(.max('h18)) counter_6 (
    .carry(counter_6_carry), .clk(or_3_out), .clr(counter_6_carry));  // open: load, D, count, Q
  Counter #(.width(4), .max('h2)) counter_7 (
    .Q(out_3), .clk(counter_5_carry), .clr(counter_6_carry));  // open: load, D, count, carry
endmodule
