// Logisim project Auto_mang.circ as structural Verilog: 1 circuit, main circuit main
module main (
  input  [7:0] in_1,
  input  [7:0] in_2,
  input  [7:0] in_3,
  input  [7:0] in_4
);

  DotMatrix #(.inputtype("row"), .matrixcols(8), .matrixrows(8), .dotshape("circle")) dotmatrix_1 (
    .row4(in_1), .row5(in_2), .row6(in_3), .row7(in_4));  // open: row0, row1, row2, row3
endmodule
