// Logisim project SA17Kalkulaator.circ as structural Verilog: 5 circuits, main circuit main
module main (
);

  wire _0_out, _1_out, _2_out, _3_out, _4_out, _5_out, _6_out, _7_out, _8_out, _9_out, button_2_out,
       button_3_out, button_4_out, button_out, C_out, keyboard_1_nupuvajutus, tehted_1_miinus,
       tehted_1_out_9, tehted_1_reset, x_out;
  wire [31:0] adder_1_out, display_1_out_2, keyboard_1_out_12, keyboard_1_out_13, not_1_out, select_1_out,
       select_2_out, \tehted_1_väljund ;

  Button _2 (.out(_2_out));
  Button _1 (.out(_1_out));
  Button _3 (.out(_3_out));
  Button _4 (.out(_4_out));
  Button _5 (.out(_5_out));
  Button _7 (.out(_7_out));
  Button _6 (.out(_6_out));
  KEYBOARD keyboard_1 (
    .out_12(keyboard_1_out_12), ._1(_1_out), ._2(_2_out), ._3(_3_out), ._4(_4_out), ._5(_5_out), ._6(_6_out),
    ._7(_7_out), ._8(_8_out), ._9(_9_out), ._0(_0_out), .RESET(tehted_1_reset),
    .NUPUVAJUTUS(keyboard_1_nupuvajutus), .out_13(keyboard_1_out_13));
  Button button (.out(button_out));
  Button _8 (.out(_8_out));
  Button _0 (.out(_0_out));
  Button _9 (.out(_9_out));
  Button button_2 (.out(button_2_out));
  Button x (.out(x_out));
  Button button_3 (.out(button_3_out));
  Button button_4 (.out(button_4_out));
  TEHTED tehted_1 (
    .\VÄLJUND (\tehted_1_väljund ), .MIINUS(tehted_1_miinus), .SISEND(keyboard_1_out_12), .in_1(button_out),
    .in_2(button_4_out), .x(x_out), .in_4(button_2_out), .in_5(button_3_out), .C(C_out),
    .RESET(tehted_1_reset), .NUPUVAJUTUS(keyboard_1_nupuvajutus), .out_9(tehted_1_out_9));
  Button C (.out(C_out));
  assign not_1_out = ~\tehted_1_väljund ;  // NOT_Gate not_1, 32 bits wide
  Adder #(.width(32)) adder_1 (.a(not_1_out), .b(32'h1), .out(adder_1_out));  // open: cin, cout
  SELECT select_1 (.SELECT(tehted_1_out_9), .A(keyboard_1_out_13), .B(select_2_out), .OUT(select_1_out));
  SELECT select_2 (.SELECT(tehted_1_miinus), .A(\tehted_1_väljund ), .B(adder_1_out), .OUT(select_2_out));
  LED led_1 (.in(tehted_1_miinus));
  Hex_Digit_Display hex_digit_display_1 (.value(display_1_out_2[31:28]));  // open: dp
  DISPLAY display_1 (.in_1(select_1_out), .out_2(display_1_out_2));
  Hex_Digit_Display hex_digit_display_2 (.value(display_1_out_2[27:24]));  // open: dp
  Hex_Digit_Display hex_digit_display_3 (.value(display_1_out_2[23:20]));  // open: dp
  Hex_Digit_Display hex_digit_display_4 (.value(display_1_out_2[15:12]));  // open: dp
  Hex_Digit_Display hex_digit_display_5 (.value(display_1_out_2[19:16]));  // open: dp
  Hex_Digit_Display hex_digit_display_6 (.value(display_1_out_2[7:4]));  // open: dp
  Hex_Digit_Display hex_digit_display_7 (.value(display_1_out_2[11:8]));  // open: dp
  Hex_Digit_Display hex_digit_display_8 (.value(display_1_out_2[3:0]));  // open: dp
endmodule

// DSP
module DISPLAY (
  input  [31:0] in_1,
  output [31:0] out_2
);

  wire [31:0] adder_1_out, adder_2_out, adder_3_out, adder_4_out, adder_5_out, adder_6_out, divider_1_out,
       divider_2_out, divider_3_out, divider_4_out, divider_5_out, divider_6_out, divider_7_out,
       multiplier_1_out, multiplier_2_out, multiplier_3_out, multiplier_4_out, multiplier_5_out,
       multiplier_6_out, multiplier_7_out;

  Divider #(.width(32)) divider_1 (.a(in_1), .b(32'ha), .out(divider_1_out));  // open: upper, rem
  Divider #(.width(32)) divider_2 (.a(in_1), .b(32'h64), .out(divider_2_out));  // open: upper, rem
  Divider #(.width(32)) divider_3 (.a(in_1), .b(32'h3e8), .out(divider_3_out));  // open: upper, rem
  Divider #(.width(32)) divider_4 (.a(in_1), .b(32'h2710), .out(divider_4_out));  // open: upper, rem
  Divider #(.width(32)) divider_5 (.a(in_1), .b(32'h186a0), .out(divider_5_out));  // open: upper, rem
  Divider #(.width(32)) divider_6 (.a(in_1), .b(32'hf4240), .out(divider_6_out));  // open: upper, rem
  Divider #(.width(32)) divider_7 (.a(in_1), .b(32'h989680), .out(divider_7_out));  // open: upper, rem
  Multiplier #(.width(32)) multiplier_1 (.a(divider_1_out), .b(32'h6), .out(multiplier_1_out));  // open: cin, cout
  Multiplier #(.width(32)) multiplier_2 (.a(divider_2_out), .b(32'h60), .out(multiplier_2_out));  // open: cin, cout
  Multiplier #(.width(32)) multiplier_3 (.a(divider_3_out), .b(32'h600), .out(multiplier_3_out));  // open: cin, cout
  Multiplier #(.width(32)) multiplier_4 (.a(divider_4_out), .b(32'h6000), .out(multiplier_4_out));  // open: cin, cout
  Multiplier #(.width(32)) multiplier_5 (.a(divider_5_out), .b(32'h60000), .out(multiplier_5_out));  // open: cin, cout
  Multiplier #(.width(32)) multiplier_6 (.a(divider_6_out), .b(32'h600000), .out(multiplier_6_out));  // open: cin, cout
  Multiplier #(.width(32)) multiplier_7 (
    .a(divider_7_out), .b(32'h6000000), .out(multiplier_7_out));  // open: cin, cout
  Adder #(.width(32)) adder_1 (.a(in_1), .b(multiplier_1_out), .out(adder_1_out));  // open: cin, cout
  Adder #(.width(32)) adder_2 (.a(adder_1_out), .b(multiplier_2_out), .out(adder_2_out));  // open: cin, cout
  Adder #(.width(32)) adder_3 (.a(adder_2_out), .b(multiplier_3_out), .out(adder_3_out));  // open: cin, cout
  Adder #(.width(32)) adder_4 (.a(adder_3_out), .b(multiplier_4_out), .out(adder_4_out));  // open: cin, cout
  Adder #(.width(32)) adder_5 (.a(adder_4_out), .b(multiplier_5_out), .out(adder_5_out));  // open: cin, cout
  Adder #(.width(32)) adder_6 (.a(adder_5_out), .b(multiplier_6_out), .out(adder_6_out));  // open: cin, cout
  Adder #(.width(32)) adder_7 (.a(adder_6_out), .b(multiplier_7_out), .out(out_2));  // open: cin, cout
endmodule

module KEYBOARD (
  input  _1,
  input  _2,
  input  _3,
  input  _4,
  input  _5,
  input  _6,
  input  _7,
  input  _8,
  input  _9,
  input  _0,
  input  RESET,
  output [31:0] out_12,
  output [31:0] out_13,
  output NUPUVAJUTUS
);

  wire [3:0] or_5_out;
  wire [31:0] adder_1_out, adder_2_out, adder_3_out, adder_4_out, adder_5_out, adder_6_out,
       bit_extender_1_out, multiplier_1_out, multiplier_2_out, multiplier_3_out, multiplier_4_out,
       multiplier_5_out, multiplier_6_out, multiplier_7_out, shift_register_1_q0, shift_register_1_q1,
       shift_register_1_q2, shift_register_1_q3, shift_register_1_q4, shift_register_1_q5,
       shift_register_1_q6, shift_register_1_q7;

  or or_1 (NUPUVAJUTUS, _1, _2, _3, _4, _5, _6, _7, _8, _9, _0);
  or or_2 (or_5_out[3], _9, _8);
  or or_3 (or_5_out[2], _7, _6, _5, _4);
  or or_4 (or_5_out[1], _7, _6, _3, _2);
  or or_5 (or_5_out[0], _9, _7, _5, _3, _1);
  Shift_Register #(.width(32), .trigger("falling")) shift_register_1 (
    .in(bit_extender_1_out), .clk(NUPUVAJUTUS), .clr(RESET), .q0(shift_register_1_q0),
    .q1(shift_register_1_q1), .q2(shift_register_1_q2), .q3(shift_register_1_q3), .q4(shift_register_1_q4),
    .q5(shift_register_1_q5), .q6(shift_register_1_q6), .q7(shift_register_1_q7));  // open: shift, out, load, d0, d1, d2, d3, d4, d5, d6, d7
  assign bit_extender_1_out = {{28{1'b0}}, or_5_out};  // Bit_Extender bit_extender_1
  Multiplier #(.width(32)) multiplier_1 (
    .a(shift_register_1_q1), .b(32'ha), .out(multiplier_1_out));  // open: cin, cout
  Multiplier #(.width(32)) multiplier_2 (
    .a(shift_register_1_q2), .b(32'h64), .out(multiplier_2_out));  // open: cin, cout
  Multiplier #(.width(32)) multiplier_3 (
    .a(shift_register_1_q3), .b(32'h3e8), .out(multiplier_3_out));  // open: cin, cout
  Multiplier #(.width(32)) multiplier_4 (
    .a(shift_register_1_q4), .b(32'h2710), .out(multiplier_4_out));  // open: cin, cout
  Multiplier #(.width(32)) multiplier_5 (
    .a(shift_register_1_q5), .b(32'h186a0), .out(multiplier_5_out));  // open: cin, cout
  Multiplier #(.width(32)) multiplier_6 (
    .a(shift_register_1_q6), .b(32'hf4240), .out(multiplier_6_out));  // open: cin, cout
  Multiplier #(.width(32)) multiplier_7 (
    .a(shift_register_1_q7), .b(32'h989680), .out(multiplier_7_out));  // open: cin, cout
  Adder #(.width(32)) adder_1 (.a(shift_register_1_q0), .b(multiplier_1_out), .out(adder_1_out));  // open: cin, cout
  Adder #(.width(32)) adder_2 (.a(adder_1_out), .b(multiplier_2_out), .out(adder_2_out));  // open: cin, cout
  Adder #(.width(32)) adder_3 (.a(adder_2_out), .b(multiplier_3_out), .out(adder_3_out));  // open: cin, cout
  Adder #(.width(32)) adder_4 (.a(adder_3_out), .b(multiplier_4_out), .out(adder_4_out));  // open: cin, cout
  Adder #(.width(32)) adder_5 (.a(adder_4_out), .b(multiplier_5_out), .out(adder_5_out));  // open: cin, cout
  Adder #(.width(32)) adder_6 (.a(adder_5_out), .b(multiplier_6_out), .out(adder_6_out));  // open: cin, cout
  Adder #(.width(32)) adder_7 (.a(adder_6_out), .b(multiplier_7_out), .out(out_12));  // open: cin, cout

  assign out_13 = out_12;
endmodule

module TEHTED (
  input  in_1,
  input  in_2,
  input  x,
  input  in_4,
  input  in_5,
  input  C,
  input  [31:0] SISEND,
  input  NUPUVAJUTUS,
  output out_9,
  output RESET,
  output [31:0] \VÄLJUND ,
  output MIINUS
);

  wire and_6_out, or_1_out, or_3_out, subtractor_1_bout, t_ff_1_q, t_ff_2_q, t_ff_3_q, t_ff_4_q;
  wire [31:0] adder_1_out, and_2_out, and_3_out, and_4_out, and_5_out, bit_extender_1_out,
       bit_extender_2_out, bit_extender_3_out, bit_extender_4_out, divider_1_out, multiplier_1_out,
       shift_register_1_q0, shift_register_1_q1, subtractor_1_out;

  Shift_Register #(.width(32), .length(2)) shift_register_1 (
    .in(SISEND), .clk(or_1_out), .clr(or_3_out), .q0(shift_register_1_q0), .q1(shift_register_1_q1));  // open: shift, out, load, d0, d1
  or or_1 (or_1_out, in_1, in_2, x, in_4, in_5);
  or or_2 (RESET, or_1_out, or_3_out);
  Adder #(.width(32)) adder_1 (.a(shift_register_1_q1), .b(shift_register_1_q0), .out(adder_1_out));  // open: cin, cout
  Subtractor #(.width(32)) subtractor_1 (
    .a(shift_register_1_q1), .b(shift_register_1_q0), .out(subtractor_1_out), .bout(subtractor_1_bout));  // open: bin
  Multiplier #(.width(32)) multiplier_1 (
    .a(shift_register_1_q1), .b(shift_register_1_q0), .out(multiplier_1_out));  // open: cin, cout
  Divider #(.width(32)) divider_1 (
    .a(shift_register_1_q1), .b(shift_register_1_q0), .out(divider_1_out));  // open: upper, rem
  T_Flip_Flop t_ff_1 (.clk(in_1), .T(in_1), .Q(t_ff_1_q), .reset(or_3_out));  // open: Qn, preset, en
  assign bit_extender_1_out = {{31{t_ff_1_q}}, t_ff_1_q};  // Bit_Extender bit_extender_1
  T_Flip_Flop t_ff_2 (.clk(in_2), .T(in_2), .Q(t_ff_2_q), .reset(or_3_out));  // open: Qn, preset, en
  assign bit_extender_2_out = {{31{t_ff_2_q}}, t_ff_2_q};  // Bit_Extender bit_extender_2
  and and_1 (MIINUS, t_ff_2_q, subtractor_1_bout);
  T_Flip_Flop t_ff_3 (.clk(x), .T(x), .Q(t_ff_3_q), .reset(or_3_out));  // open: Qn, preset, en
  assign bit_extender_3_out = {{31{t_ff_3_q}}, t_ff_3_q};  // Bit_Extender bit_extender_3
  T_Flip_Flop t_ff_4 (.clk(in_4), .T(in_4), .Q(t_ff_4_q), .reset(or_3_out));  // open: Qn, preset, en
  assign bit_extender_4_out = {{31{t_ff_4_q}}, t_ff_4_q};  // Bit_Extender bit_extender_4
  T_Flip_Flop t_ff_5 (.clk(in_5), .T(in_5), .Q(out_9), .reset(or_3_out));  // open: Qn, preset, en
  or or_3 (or_3_out, C, and_6_out);
  assign and_2_out = adder_1_out & bit_extender_1_out;  // AND_Gate and_2, 32 bits wide
  assign and_3_out = subtractor_1_out & bit_extender_2_out;  // AND_Gate and_3, 32 bits wide
  assign and_4_out = multiplier_1_out & bit_extender_3_out;  // AND_Gate and_4, 32 bits wide
  assign and_5_out = divider_1_out & bit_extender_4_out;  // AND_Gate and_5, 32 bits wide
  and and_6 (and_6_out, out_9, NUPUVAJUTUS);
  assign \VÄLJUND  = and_2_out | and_3_out | and_4_out | and_5_out;  // OR_Gate or_4, 32 bits wide
endmodule

// SEL
module SELECT (
  input  SELECT,
  input  [31:0] A,
  input  [31:0] B,
  output [31:0] OUT
);

  wire [31:0] and_1_out, and_2_out, bit_extender_1_out, not_1_out;

  assign bit_extender_1_out = {{31{SELECT}}, SELECT};  // Bit_Extender bit_extender_1
  assign not_1_out = ~bit_extender_1_out;  // NOT_Gate not_1, 32 bits wide
  assign and_1_out = not_1_out & A;  // AND_Gate and_1, 32 bits wide
  assign and_2_out = bit_extender_1_out & B;  // AND_Gate and_2, 32 bits wide
  assign OUT = and_1_out | and_2_out;  // OR_Gate or_1, 32 bits wide
endmodule
